# Fritzing sketch raspi-fan (saved by Fritzing 0.9.3b)
circuit board: 0.950611cm x 2.8cm
breadboards: 1

parts:
  Raspberry_Pi_1 = Raspberry Pi 3 [part_number=RPI-3-V1.2]  # not connected
  T1 = NPN-Transistor [package="TO92 [THT]"]
  3V3 = female pin header, 1 pin [form="♀ (female)"]
  -5V = female pin header, 1 pin [form="♀ (female)"]
  - = female pin header, 1 pin [form="♀ (female)"]
  + = female pin header, 1 pin [form="♀ (female)"]
  D1 = Rectifier Diode [part_number=1N4001 package="300 mil [THT]"]
  +5V = female pin header, 1 pin [form="♀ (female)"]
  R1 = Resistor [tolerance=±5% resistance=1k package=THT]

nets:
  N1: T1.E, -5V.pin1
  N2: T1.B, R1.Pin_1
  N3: T1.C, -.pin1, D1.anode
  N4: 3V3.pin1, R1.Pin_0
  N5: +.pin1, D1.cathode, +5V.pin1

notes:
  1.15.0
